# Fritzing sketch Button Matrix (saved by Fritzing 0.9.5d)

parts:
  S1 = Pushbutton [package="[THT]"]
  S2 = Pushbutton [package="[THT]"]
  S3 = Pushbutton [package="[THT]"]
  S4 = Pushbutton [package="[THT]"]
  S5 = Pushbutton [package="[THT]"]
  S6 = Pushbutton [package="[THT]"]
  S7 = Pushbutton [package="[THT]"]  # not connected
  S8 = Pushbutton [package="[THT]"]  # not connected
  S9 = Pushbutton [package="[THT]"]  # not connected
  S10 = Pushbutton [package="[THT]"]  # not connected
  S11 = Pushbutton [package="[THT]"]
  S12 = Pushbutton [package="[THT]"]  # not connected
  S13 = Pushbutton [package="[THT]"]  # not connected
  S14 = Pushbutton [package="[THT]"]  # not connected
  S15 = Pushbutton [package="[THT]"]  # not connected
  S16 = Pushbutton [package="[THT]"]
  S17 = Pushbutton [package="[THT]"]  # not connected
  S18 = Pushbutton [package="[THT]"]  # not connected
  S19 = Pushbutton [package="[THT]"]  # not connected
  S20 = Pushbutton [package="[THT]"]  # not connected
  MCU1 = Raspberry Pi Zero

nets:
  N1: S1.Pin_1, S1.Pin_2, MCU1.pin_22
  N2: S1.Pin_3, S1.Pin_4, MCU1.pin_29
  N3: S2.Pin_2, MCU1.pin_24
  N4: S3.Pin_2, MCU1.pin_26
  N5: S4.Pin_2, MCU1.pin_32
  N6: S5.Pin_2, MCU1.pin_36
  N7: S6.Pin_4, MCU1.pin_31
  N8: S11.Pin_4, MCU1.pin_33
  N9: S16.Pin_4, MCU1.pin_35
