# Fritzing sketch I2C Display (saved by Fritzing 0.9.5d)

parts:
  LCM1602_IIC1 = LCM1602 IIC [part_number="LCM1602 IIC" chip_label="LCM1602 IIC" package="DIP (Dual Inline) [THT]"]
  MCU1 = Raspberry Pi Zero

nets:
  N1: LCM1602_IIC1.GND, MCU1.pin_6, MCU1.pin_39
  N2: LCM1602_IIC1.VCC, MCU1.pin_1, MCU1.pin_17
  N3: LCM1602_IIC1.SDA, MCU1.pin_3
  N4: LCM1602_IIC1.SCL, MCU1.pin_5

custom parts:
  LCM1602 IIC: I2C-Module to use a 1602 or 2004 LCD on with the wire.h libory Serial LCD Modul
